// Logisim project SPRINT 1.circ as structural Verilog: 1 circuit, main circuit main
module main (
  input  A,
  input  B,
  input  C,
  input  D,
  input  E,
  input  F,
  output A7,
  output A4,
  output A2
);

  wire and_1_out, and_2_out, and_3_out, and_4_out, and_5_out, and_6_out, and_7_out, and_8_out, or_1_out,
       or_2_out, or_3_out, xor_1_out, xor_2_out, xor_3_out, xor_4_out, xor_5_out, xor_6_out;

  xor xor_1 (xor_1_out, A, B);
  and and_1 (and_1_out, B, A);
  xor xor_2 (xor_2_out, D, E);
  and and_2 (and_2_out, E, D);
  xor xor_3 (xor_3_out, xor_1_out, C);
  and and_3 (and_3_out, C, xor_1_out);
  xor xor_4 (xor_4_out, xor_2_out, F);
  and and_4 (and_4_out, F, xor_2_out);
  or or_1 (or_1_out, and_3_out, and_1_out);
  or or_2 (or_2_out, and_4_out, and_2_out);
  xor xor_5 (xor_5_out, xor_3_out, xor_4_out);
  and and_5 (and_5_out, xor_4_out, xor_3_out);
  xor xor_6 (xor_6_out, or_2_out, or_1_out);
  and and_6 (and_6_out, or_2_out, or_1_out);
  xor xor_7 (A7, xor_5_out, 1'b0);
  and and_7 (and_7_out, xor_5_out, 1'b0);
  or or_3 (or_3_out, and_7_out, and_5_out);
  and and_8 (and_8_out, xor_6_out, or_3_out);
  xor xor_8 (A4, or_3_out, xor_6_out);
  or or_4 (A2, and_8_out, and_6_out);
endmodule
